// Logisim project Project2Given.circ as structural Verilog: 4 circuits, main circuit main
module main (
);

  wire and_1_out, and_2_out, B0, B1, B2, B3, B4, B5, B6, B7, B8, B9, BL, BU, C0, C1, C2, CLK, L1_l, L1_u,
       not_1_out, or_8_out, P1_v, R0, R1, R3, R4, Valid;
  wire [2:0] counter_1_q;
  wire [3:0] IB1_c0, P1_b0, register_3_q, register_4_q, register_5_q;

  Button n1 (.out(B1));
  Button n4 (.out(B4));
  Button n7 (.out(B7));
  Button L (.out(BL));
  Button n3 (.out(B3));
  Button n2 (.out(B2));
  Button n6 (.out(B6));
  Button n5 (.out(B5));
  Button n9 (.out(B9));
  Button n8 (.out(B8));
  Button U (.out(BU));
  Button n0 (.out(B0));
  or or_1 (R0, B3, B2, B1);
  or or_2 (R1, B6, B5, B4);
  or or_3 (R3, B9, B8, B7);
  or or_4 (R4, BU, B0, BL);
  or or_5 (C0, B1, B4, B7, BL);
  or or_6 (C1, B2, B5, B8, B0);
  or or_7 (C2, B3, B6, B9, BU);
  Clock clock_1 (.out(CLK));
  nand nand_1 (Valid, IB1_c0[0], IB1_c0[1], IB1_c0[2], IB1_c0[3]);
  // Probe on P1_b0
  Panel P1 (
    .R0(R0), .R1(R1), .R2(R3), .R3(R4), .C0(C0), .C1(C1), .C2(C2), .B0(P1_b0[0]), .B1(P1_b0[1]),
    .B2(P1_b0[2]), .B3(P1_b0[3]), .V(P1_v));
  LED Press (.in(P1_v));
  // Probe on IB1_c0
  InputBuffer IB1 (
    .B0(P1_b0[0]), .B1(P1_b0[1]), .B2(P1_b0[2]), .B3(P1_b0[3]), .V(P1_v), .CLK(not_1_out), .C0(IB1_c0[0]),
    .C1(IB1_c0[1]), .C2(IB1_c0[2]), .C3(IB1_c0[3]));
  not not_1 (not_1_out, CLK);
  Register #(.width(4)) register_1 (.D(register_3_q), .en(Valid), .clk(CLK));  // open: Q, clr
  Lock L1 (.C0(IB1_c0[0]), .C1(IB1_c0[1]), .C2(IB1_c0[2]), .C3(IB1_c0[3]), .CLK(CLK), .L(L1_l), .U(L1_u));
  Counter #(.max('h7), .width(3)) counter_1 (
    .count(or_8_out), .Q(counter_1_q), .up(L1_u), .clk(CLK));  // open: load, D, carry, clr
  or or_8 (or_8_out, L1_l, L1_u);
  Register #(.width(4)) register_2 (.D(register_3_q), .en(Valid), .clk(CLK));  // open: Q, clr
  LED Unlocked (.in(and_1_out));
  and and_1 (and_1_out, ~counter_1_q[0], ~counter_1_q[1], ~counter_1_q[2]);  // AND_Gate
  Register #(.width(4)) register_3 (.D(register_4_q), .en(Valid), .clk(CLK), .Q(register_3_q));  // open: clr
  LED Locked (.in(and_2_out));
  and and_2 (and_2_out, ~counter_1_q[0], ~counter_1_q[1], counter_1_q[2]);  // AND_Gate
  Register #(.width(4)) register_4 (.D(register_5_q), .en(Valid), .clk(CLK), .Q(register_4_q));  // open: clr
  Register #(.width(4)) register_5 (.D(IB1_c0), .en(Valid), .clk(CLK), .Q(register_5_q));  // open: clr
endmodule

module Panel (
  input  R0,
  input  R1,
  input  R2,
  input  R3,
  input  C0,
  input  C1,
  input  C2,
  output B0,
  output B1,
  output B2,
  output B3,
  output V
);

  wire and_1_out, and_2_out, and_3_out, and_4_out, and_5_out, and_6_out, and_7_out, and_8_out, and_9_out,
       and_10_out, and_11_out, and_12_out, and_13_out, and_14_out, and_15_out, and_16_out, and_17_out,
       and_18_out, and_19_out, and_21_out, and_22_out, and_23_out, and_24_out, and_25_out, and_26_out,
       and_27_out, and_28_out, and_29_out, and_30_out, and_31_out, and_32_out, and_33_out, xor_1_out,
       xor_2_out;

  and and_1 (and_1_out, R0, C0);
  and and_2 (and_2_out, R0, C2);
  and and_3 (and_3_out, R1, C1);
  and and_4 (and_4_out, R2, C0);
  and and_5 (and_5_out, R2, C2);
  and and_6 (and_6_out, R3, C1);
  and and_7 (and_7_out, R3, C2);
  and and_8 (and_8_out, C1, R2);
  and and_9 (and_9_out, R2, C2);
  and and_10 (and_10_out, R3, C0);
  and and_11 (and_11_out, R3, C1);
  and and_12 (and_12_out, R3, C2);
  or or_1 (B3, and_8_out, and_9_out, and_10_out, and_11_out, and_12_out);
  or or_2 (B0, and_1_out, and_2_out, and_3_out, and_4_out, and_5_out, and_6_out, and_7_out);
  and and_13 (and_13_out, R0, C1);
  and and_14 (and_14_out, R0, C2);
  and and_15 (and_15_out, R1, C2);
  and and_16 (and_16_out, R2, C0);
  and and_17 (and_17_out, R3, C0);
  and and_18 (and_18_out, R3, C1);
  and and_19 (and_19_out, R3, C2);
  ExactlyOne xor_1 (.out(xor_1_out), .in0(R0), .in1(R1), .in2(R2), .in3(R3));
  ExactlyOne xor_2 (.out(xor_2_out), .in0(C2), .in1(C1), .in2(C0));
  and and_20 (V, xor_1_out, xor_2_out);
  or or_3 (B1, and_13_out, and_14_out, and_15_out, and_16_out, and_17_out, and_18_out, and_19_out);
  and and_21 (and_21_out, R0, R1);
  and and_22 (and_22_out, R0, R2);
  and and_23 (and_23_out, R0, R3);
  and and_24 (and_24_out, R1, R2);
  and and_25 (and_25_out, R1, R3);
  and and_26 (and_26_out, R1, R3);
  and and_27 (and_27_out, C0, C1);
  and and_28 (and_28_out, C0, C2);
  and and_29 (and_29_out, C1, C2);
  // OR_Gate or_4 has open pins: in0=and_21_out, in1=and_22_out, in2=and_23_out, in3=and_24_out, in4=and_25_out, in5=and_26_out, out=open
  // NOR_Gate nor_1 is placed but not wired
  and and_30 (and_30_out, C0, R1);
  and and_31 (and_31_out, C1, R1);
  and and_32 (and_32_out, R1, C2);
  and and_33 (and_33_out, R2, C0);
  or or_5 (B2, and_30_out, and_31_out, and_32_out, and_33_out);
endmodule

module InputBuffer (
  input  B0,
  input  B1,
  input  B2,
  input  B3,
  input  V,
  input  CLK,
  output C0,
  output C1,
  output C2,
  output C3
);

  wire and_1_out, and_2_out, and_3_out, and_4_out, multiplexer_1_out, not_1_out, or_1_out, S0_q, S0_qn, S1_q,
       S1_qn;

  and and_1 (and_1_out, V, S1_q, ~S0_q);  // AND_Gate
  and and_2 (and_2_out, S0_q, ~S1_q, V);  // AND_Gate
  and and_3 (and_3_out, ~S0_q, ~S1_q, V);  // AND_Gate
  D_Flip_Flop S1 (.D(or_1_out), .clk(CLK), .Q(S1_q), .Qn(S1_qn));  // open: preset, reset
  or or_1 (or_1_out, and_1_out, and_2_out);
  D_Flip_Flop S0 (.D(and_3_out), .clk(CLK), .Q(S0_q), .Qn(S0_qn));  // open: preset, reset
  and and_4 (and_4_out, V, S1_qn);
  not not_1 (not_1_out, S0_qn);
  Multiplexer multiplexer_1 (.in0(S0_qn), .in1(not_1_out), .out(multiplexer_1_out), .sel(and_4_out));
  or or_2 (C0, B0, multiplexer_1_out);
  or or_3 (C1, B1, multiplexer_1_out);
  or or_4 (C2, B2, multiplexer_1_out);
  or or_5 (C3, B3, multiplexer_1_out);
endmodule

module Lock (
  input  C0,
  input  C1,
  input  C2,
  input  C3,
  input  CLK,
  output L,
  output U
);

  wire and_1_out, and_2_out, and_3_out, and_4_out, and_5_out, and_6_out, and_7_out, and_8_out, and_9_out,
       and_10_out, and_11_out, and_12_out, and_13_out, and_14_out, not_1_out, not_2_out, not_3_out,
       not_4_out, or_1_out, or_2_out, or_3_out, S0_q, S0_qn, S1_q, S1_qn, S2_q, S2_qn;

  not not_1 (not_1_out, C0);
  not not_2 (not_2_out, C1);
  not not_3 (not_3_out, C2);
  not not_4 (not_4_out, C3);
  and and_1 (and_1_out, not_1_out, C1, not_3_out, C3, S0_qn, S1_qn, S2_qn);
  and and_2 (and_2_out, C0, C1, C3, C2, S0_q, S1_qn, S2_qn);
  and and_3 (and_3_out, S2_qn, S1_qn, S0_q, not_3_out, not_2_out, not_4_out, not_1_out);
  and and_4 (and_4_out, S2_qn, S0_qn, S1_q, C3, not_3_out, C1, not_1_out);
  and and_5 (and_5_out, S2_q, S1_qn, S0_qn, C0, C1, C2, C3);
  and and_6 (and_6_out, S2_q, S1_qn, S0_qn, not_1_out, not_2_out, not_3_out, not_4_out);
  and and_7 (and_7_out, S2_q, S1_qn, S0_qn, C3, not_3_out, C1, not_1_out);
  and and_8 (and_8_out, S2_q, S1_qn, S0_q, C3, not_3_out, C1, C0);
  and and_9 (and_9_out, S1_q, S0_q, S2_qn, C0, C1, C2, C3);
  and and_10 (and_10_out, S1_q, S0_q, S2_qn, not_1_out, not_4_out, not_2_out, not_3_out);
  and and_11 (and_11_out, S2_q, S1_qn, S0_qn, not_4_out, not_1_out, not_2_out, not_3_out);
  or or_1 (or_1_out, and_1_out, and_2_out, and_3_out, and_4_out, and_5_out, and_6_out);
  or or_2 (or_2_out, and_7_out, and_2_out, and_3_out, and_8_out);
  or or_3 (or_3_out, and_9_out, and_10_out, and_11_out, and_5_out, and_8_out);
  D_Flip_Flop S0 (.D(or_1_out), .clk(CLK), .Q(S0_q), .Qn(S0_qn));  // open: preset, reset
  D_Flip_Flop S1 (.D(or_2_out), .clk(CLK), .Q(S1_q), .Qn(S1_qn), .preset(S1_q));  // open: reset
  D_Flip_Flop S2 (.D(or_3_out), .clk(CLK), .Q(S2_q), .Qn(S2_qn));  // open: preset, reset
  and and_12 (and_12_out, S2_q, S1_qn, S0_qn);
  and and_13 (and_13_out, S0_q, S1_q, S2_qn);
  and and_14 (and_14_out, S0_qn, S1_q, S2_qn);
  or or_4 (L, and_12_out, and_13_out, and_14_out);
endmodule
